# Fritzing sketch led_chaser_game (saved by Fritzing 0.9.3b)
breadboards: 1

parts:
  Raspberry_Pi_1 = Raspberry Pi 3 [part_number=RPI-3-V1.2]  # not connected
  GPIO_Expansion_Shield_Wire1 = GPIO_Expansion_Shield_Wire  # not connected
  Raspberry_Pi_GPIO_Expansion_Shield1 = Raspberry Pi GPIO Expansion Shield (Blue)
  S1 = Pushbutton [package="[THT]"]
  R2 = Resistor [tolerance=±5% resistance=220 package=THT]
  R3 = Resistor [tolerance=±5% resistance=1k package=THT]
  LED2 = LED - 5mm [color="Red (633nm)" package="5 mm [THT]"]
  LED3 = LED - 5mm [color="Green (560nm)" package="5 mm [THT]"]
  LED4 = LED - 5mm [color="Green (560nm)" package="5 mm [THT]"]
  LED5 = LED - 5mm [color="Blue (505nm)" package="5 mm [THT]"]
  LED6 = LED - 5mm [color="Blue (505nm)" package="5 mm [THT]"]
  R4 = Resistor [tolerance=±5% resistance=220 package=THT]
  R5 = Resistor [tolerance=±5% resistance=220 package=THT]
  R6 = Resistor [tolerance=±5% resistance=220 package=THT]
  R7 = Resistor [tolerance=±5% resistance=220 package=THT]

nets:
  3V3: Raspberry_Pi_GPIO_Expansion_Shield1.3v3, Raspberry_Pi_GPIO_Expansion_Shield1.3V3
  N1: Raspberry_Pi_GPIO_Expansion_Shield1.GND, R2.Pin_1, R3.Pin_1, R4.Pin_1, R5.Pin_1, R6.Pin_1, R7.Pin_1
  N2: Raspberry_Pi_GPIO_Expansion_Shield1.GIPO13, S1.Pin_1, S1.Pin_2
  N3: Raspberry_Pi_GPIO_Expansion_Shield1.GIPO26, LED5.anode
  N4: Raspberry_Pi_GPIO_Expansion_Shield1.GIPO21, LED3.anode
  N5: Raspberry_Pi_GPIO_Expansion_Shield1.GIPO20, LED2.anode
  N6: Raspberry_Pi_GPIO_Expansion_Shield1.GIPO16, LED4.anode
  N7: Raspberry_Pi_GPIO_Expansion_Shield1.GIPO12, LED6.anode
  N8: S1.Pin_3, S1.Pin_4, R3.Pin_0
  N9: R2.Pin_0, LED6.cathode
  N10: LED2.cathode, R5.Pin_0
  N11: LED3.cathode, R6.Pin_0
  N12: LED4.cathode, R4.Pin_0
  N13: LED5.cathode, R7.Pin_0
